// Digital circuit CPLD-MAIN.dig as structural Verilog
module CPLD_MAIN (
  input  GCLK,
  input  nRST,
  input  [1:0] FT_RT,
  input  RnW,
  input  [15:0] AI,
  input  VDA,
  input  VPA,
  input  nIRQ_VIA,
  input  nIRQ_EXT,
  input  nWSE_INP,
  input  VIA_T1,
  input  [7:0] AD,
  input  PHI1,
  output [7:0] MD,
  output [7:0] BANK_O,
  output nOE_MEM,
  output nWE_MEM,
  output nCS_RAM0,
  output nCS_ROM,
  output nIOE,
  output nRDFT,
  output WRFT,
  output nIRQ_O,
  output nCS_EXT,
  output nCS_VIA,
  output nCS_RAM1,
  output nWSE
);

  wire and_8_out, and_9_out, and_10_out, d_ff_1_nq, d_ff_2_q, d_ff_3_q, jk_ff_1_nq, nand_3_out, nand_4_out,
       nand_6_out, nand_7_out, nC, nor_1_out, or_2_out, or_3_out, or_5_out, or_6_out, or_7_out, or_8_out,
       or_9_out, or_10_out, R, RD_C, RD_FT, RD_IO, RD_LFSR, RD_ST, VA, WR_C, WR_IO, WR_ST;
  wire [2:0] D_ST;
  wire [3:3] CONTROL_q;
  wire [5:0] T1MUL_out;
  wire [7:0] D_CPU, lfsr_1_q, multiplexer_1_out, multiplexer_2_out;

  not not_1 (R, nRST);
  not not_2 (nC, GCLK);
  Multiplexer #(.Bits(8)) multiplexer_1 (.sel(R), .in_0(AD), .in_1({8{1'b0}}), .out(multiplexer_1_out));
  or or_1 (VA, VDA, VPA);
  or or_2 (or_2_out, R, PHI1);
  and and_1 (RD_IO, ~nIOE, RnW, ~PHI1);  // And
  and and_2 (WR_IO, ~nIOE, ~RnW, ~PHI1);  // And
  nand nand_1 (RD_C, ~PHI1, RnW);  // NAnd
  nand nand_2 (WR_C, ~PHI1, ~RnW);  // NAnd
  latch8 latch8_1 (.d(multiplexer_1_out), .ena(or_2_out), .q(BANK_O));
  Register #(.Bits(4)) CONTROL (.D(D_CPU[3:0]), .C(PHI1), .en(WR_ST), .Q({CONTROL_q[3], D_ST}));
  and and_3 (RD_ST, ~AI[0], ~AI[1], ~AI[2], ~AI[3], ~AI[4], ~AI[5], ~AI[6], ~AI[7], RD_IO);  // And
  and and_4 (WR_ST, ~AI[0], ~AI[1], ~AI[2], ~AI[3], ~AI[4], ~AI[5], ~AI[6], ~AI[7], WR_IO);  // And
  and and_5 (RD_FT, AI[0], ~AI[1], ~AI[2], ~AI[3], ~AI[4], ~AI[5], ~AI[6], ~AI[7], RD_IO);  // And
  and and_6 (WRFT, AI[0], ~AI[1], ~AI[2], ~AI[3], ~AI[4], ~AI[5], ~AI[6], ~AI[7], WR_IO);  // And
  and and_7 (RD_LFSR, ~AI[0], AI[1], ~AI[2], ~AI[3], ~AI[4], ~AI[5], ~AI[6], ~AI[7], RD_IO);  // And
  or or_3 (or_3_out, R, and_8_out);
  Counter #(.Bits(6)) T1MUL (.en(1'b1), .C(VIA_T1), .clr(or_3_out), .out(T1MUL_out));  // open: ovf
  and and_8 (and_8_out, ~T1MUL_out[0], T1MUL_out[1], ~T1MUL_out[2], ~T1MUL_out[3], T1MUL_out[4], T1MUL_out[5]);  // And
  D_FF d_ff_1 (.D(and_8_out), .C(GCLK), .nQ(d_ff_1_nq));  // open: Q
  and and_9 (and_9_out, and_8_out, d_ff_1_nq);
  D_FF d_ff_2 (.D(and_9_out), .C(GCLK), .Q(d_ff_2_q));  // open: nQ
  D_FF d_ff_3 (.D(d_ff_2_q), .C(GCLK), .Q(d_ff_3_q));  // open: nQ
  nand nand_3 (nand_3_out, AI[8], AI[9], AI[10], AI[11], AI[12], AI[13], AI[14], AI[15], ~BANK_O[0], ~BANK_O[1], ~BANK_O[2], ~BANK_O[3], ~BANK_O[4], ~BANK_O[5], ~BANK_O[6], ~BANK_O[7], VA);  // NAnd
  nand nand_4 (nand_4_out, ~AI[14], ~AI[15], BANK_O[0], ~BANK_O[1], ~BANK_O[2], ~BANK_O[3], ~BANK_O[4], ~BANK_O[5], ~BANK_O[6], ~BANK_O[7], VA);  // NAnd
  nand nand_5 (nIOE, ~AI[8], ~AI[9], ~AI[10], ~AI[11], ~AI[12], ~AI[13], ~AI[14], ~AI[15], BANK_O[0], ~BANK_O[1], ~BANK_O[2], ~BANK_O[3], ~BANK_O[4], ~BANK_O[5], ~BANK_O[6], ~BANK_O[7], VA);  // NAnd
  nor nor_1 (nor_1_out, and_9_out, d_ff_2_q, d_ff_3_q);
  and and_10 (and_10_out, nand_3_out, nand_4_out);
  nand nand_6 (nand_6_out, nIOE, nCS_ROM, VA);
  nand nand_7 (nand_7_out, nCS_ROM, nIOE, nWSE_INP);
  LFSR lfsr_1 (.C(GCLK), .Q(lfsr_1_q));
  or or_4 (nCS_ROM, and_10_out, ~nIOE);  // Or
  or or_5 (or_5_out, BANK_O[4], BANK_O[5], BANK_O[6], BANK_O[7], nand_6_out);
  or or_6 (or_6_out, ~D_ST[1], nor_1_out);  // Or
  or or_7 (or_7_out, ~D_ST[0], nIRQ_VIA);  // Or
  or or_8 (or_8_out, ~D_ST[2], nIRQ_EXT);  // Or
  Multiplexer #(.Bits(8)) multiplexer_2 (
    .sel(RD_LFSR), .in_0({FT_RT, 3'b000, D_ST}), .in_1(lfsr_1_q), .out(multiplexer_2_out));
  or or_9 (or_9_out, BANK_O[4], BANK_O[5], BANK_O[6], BANK_O[7]);
  and and_11 (nIRQ_O, or_6_out, or_7_out, or_8_out);
  JK_FF jk_ff_1 (.J(jk_ff_1_nq), .C(GCLK), .K(nand_7_out), .Q(nWSE), .nQ(jk_ff_1_nq));
  or or_10 (or_10_out, RD_ST, RD_LFSR);
  // PinControl #(.Bits(8)) pincontrol_1: pin names not known; wires that end beside it: multiplexer_2_out, or_10_out, D_CPU, MD
  or or_11 (nOE_MEM, ~nIOE, RD_C);  // Or
  or or_12 (nWE_MEM, ~nIOE, WR_C);  // Or
  nand nand_8 (nCS_EXT, VA, or_9_out);
  or or_13 (nCS_RAM0, BANK_O[3], or_5_out);
  or or_14 (nCS_RAM1, ~BANK_O[3], or_5_out);  // Or
  nand nand_9 (nCS_VIA, AI[4], ~AI[5], ~AI[6], ~AI[7], ~nIOE);  // NAnd
  not not_3 (nRDFT, RD_FT);
  // Probe on AI
  // Probe on {BANK_O, AI}

  // Other names for the same wires on the sheet: EN_VIAI = D_ST[0]; EN_T1I = D_ST[1]; EN_EXTI = D_ST[2];
  //   AO[23:0] = {BANK_O, AI}; BANK[7:0] = BANK_O; C = GCLK; C_VIA = VIA_T1; D_ST[7:6] = FT_RT; nROM = nCS_ROM;
  //   nWSE_EXT = nWSE_INP; WR_FT = WRFT

  // Notes on the sheet:
  //   MD: Data Bus IO
  //   nRST: Reset, default 1
  //   BANK_O: Bank Address Output
  //   nOE_MEM: Read Memory
  //   nWE_MEM: Write Memory
  //   FT_RT: FT240X
  //   1 - RXF
  //   0 - TXE
  //   RnW: Read/Write, default 1
  //   AI: Address Input
  //   nRDFT: Read FT240X
  //   WRFT: Write FT240X
  //   nIRQ_O: Interrupt Output
  //   VDA: Valid Data Address
  //   VPA: Valid Program Address
  //   nIRQ_VIA: Interrupt Input, default 1
  //   nIRQ_EXT: Interrupt Input, default 1
  //   nWSE_INP: default 1
  //   VIA_T1: default 1
  //   AD: CPU Address/Data Bus
  //   0x000000 - 0x00FEFF	LoRAM	(63.75kB)
  //   0x00FF00 - 0x00FFFF	LoROM	(256B)
  //   0x010000 - 0x0100FF	IO	(256B)
  //   0x010100 - 0x013FFF	HiROM	(15.75kB)
  //   0x014000 - 0x0FFFFF	HiRAM	(944kB)
  //   ...
  //   0x100000 - 0xFFFFFF	EXT	(15MB)
endmodule
