// Digital circuit LFSR.dig as structural Verilog
module LFSR (
  input  C,
  output [7:0] Q
);

  wire d_ff_1_q, d_ff_3_q, d_ff_4_q, d_ff_6_q, d_ff_7_q, d_ff_8_q, d_ff_9_q, d_ff_11_q, d_ff_13_q,
       xnor_1_out, xor_1_out, xor_2_out;

  D_FF d_ff_1 (.D(xnor_1_out), .C(C), .Q(d_ff_1_q));  // open: nQ
  xnor xnor_1 (xnor_1_out, d_ff_8_q, xor_1_out);
  D_FF d_ff_2 (.D(d_ff_1_q), .C(C), .Q(Q[2]));  // open: nQ
  D_FF d_ff_3 (.D(Q[2]), .C(C), .Q(d_ff_3_q));  // open: nQ
  D_FF d_ff_4 (.D(d_ff_3_q), .C(C), .Q(d_ff_4_q));  // open: nQ
  D_FF d_ff_5 (.D(d_ff_4_q), .C(C), .Q(Q[4]));  // open: nQ
  D_FF d_ff_6 (.D(Q[4]), .C(C), .Q(d_ff_6_q));  // open: nQ
  D_FF d_ff_7 (.D(d_ff_6_q), .C(C), .Q(d_ff_7_q));  // open: nQ
  D_FF d_ff_8 (.D(d_ff_7_q), .C(C), .Q(d_ff_8_q));  // open: nQ
  D_FF d_ff_9 (.D(d_ff_8_q), .C(C), .Q(d_ff_9_q));  // open: nQ
  D_FF d_ff_10 (.D(d_ff_9_q), .C(C), .Q(Q[7]));  // open: nQ
  xor xor_1 (xor_1_out, Q[7], xor_2_out);
  xor xor_2 (xor_2_out, d_ff_11_q, d_ff_13_q);
  D_FF d_ff_11 (.D(Q[7]), .C(C), .Q(d_ff_11_q));  // open: nQ
  D_FF d_ff_12 (.D(d_ff_11_q), .C(C), .Q(Q[0]));  // open: nQ
  xnor xnor_2 (Q[1], d_ff_8_q, d_ff_4_q);
  D_FF d_ff_13 (.D(Q[0]), .C(C), .Q(d_ff_13_q));  // open: nQ
  and and_1 (Q[6], ~d_ff_1_q, d_ff_3_q);  // And
  xor xor_3 (Q[5], d_ff_11_q, d_ff_7_q);
  not not_1 (Q[3], d_ff_9_q);

  // Notes on the sheet:
  //   C: Hz: 10
endmodule
