// Digital circuit latch.dig as structural Verilog
module latch (
  input  d,
  input  ena,
  output q
);

  wire and_1_out, and_2_out, nor_2_out;

  and and_1 (and_1_out, ~d, ena);  // And
  and and_2 (and_2_out, d, ena);
  nor nor_1 (q, and_1_out, nor_2_out);
  nor nor_2 (nor_2_out, q, and_2_out);
endmodule
