// Digital circuit latch8.dig as structural Verilog
module latch8 (
  input  [7:0] d,
  input  ena,
  output [7:0] q
);

  latch latch_1 (.d(d[0]), .ena(ena), .q(q[0]));
  latch latch_2 (.d(d[1]), .ena(ena), .q(q[1]));
  latch latch_3 (.d(d[2]), .ena(ena), .q(q[2]));
  latch latch_4 (.d(d[3]), .ena(ena), .q(q[3]));
  latch latch_5 (.d(d[4]), .ena(ena), .q(q[4]));
  latch latch_6 (.d(d[5]), .ena(ena), .q(q[5]));
  latch latch_7 (.d(d[6]), .ena(ena), .q(q[6]));
  latch latch_8 (.d(d[7]), .ena(ena), .q(q[7]));
endmodule
